# Fritzing sketch Projekt_Karty (saved by Fritzing 0.7.11b)
breadboards: 1

parts:
  Nano1 = Arduino Nano v2.3
  U1 = microSD Socket [package="Molex 502774-0891 [SMD]"]  # not connected
  Part1 = Real Time Clock Module - DS1307 RTC Breakout Board
  Part2 = Barometric Pressure Sensor - BMP085 Breakout
  Part3 = Bluetooth Mate Silver

nets:
  N1: Nano1.D1TX, Part3.RX_5V
  N2: Nano1.D0RX, Part3.TX_5V
  GND: Nano1.GND, Part1.GND, Part3.GND
  N3: Nano1.A6, Part2.SDA
  N4: Nano1.A5, Part2.SCL
  N5: Nano1.A4, Part1.SDA
  +5V: Nano1.+5V, Part1.5V, Part3.VCC
